# Fritzing sketch SchemaCapteurTemp (saved by Fritzing 0.9.3b)

parts:
  U1 = TMP36 [package=to-92-kit]
  U3 = NodeMCU V1.0

nets:
  VCC: U1.VCC, U3.3V3
  N1: U1.VOUT, U3.A0
  GND: U1.GND, U3.GND
  N2: U3.D0, U3.RST

custom parts:
  NodeMCU V1.0: ESP8266 based NodeMCU V1.0
